# Fritzing sketch Diagrama (saved by Fritzing 0.9.2b)
breadboards: 1

parts:
  Part1 = Arduino Uno (Rev3)
  S1 = Pushbutton [package="[THT]"]
  S2 = Pushbutton [package="[THT]"]
  R2 = Rotary Potentiometer (Large) [maximum_resistance=5kΩ package=THT]
  R3 = Rotary Potentiometer (Large) [maximum_resistance=5kΩ package=THT]
  R4 = Resistor [tolerance=±5% resistance=10k package=THT]
  R5 = Resistor [tolerance=±5% resistance=10k package=THT]
  Grove1 = Grove OLED 128x96

nets:
  N1: Part1.A0, R2.wiper
  N2: Part1.A1, R3.wiper
  N3: Part1.D8, S2.Pin_3, S2.Pin_4, R4.Pin_1
  N4: Part1.A4/SDA, Grove1.SDA
  N5: Part1.A5/SCL, Grove1.SCL
  N6: Part1.D7, S1.Pin_1, S1.Pin_2, R5.Pin_0
  5V: Part1.5V, R2.leg2, R3.leg1, R4.Pin_0, R5.Pin_1, Grove1.VCC
  GND: Part1.GND, S1.Pin_3, S1.Pin_4, S2.Pin_1, S2.Pin_2, R2.leg1, R3.leg2, Grove1.GND
